# Fritzing sketch fritzing_protoboard (saved by Fritzing 0.8.7b)
breadboards: 1

parts:
  SHT11 = Humidity Temperature Sensor SHT15
  Raspberry_Pi_B_rev2 = Raspberry Pi B rev2
  R1_(10k) = Resistor [tolerance=±5% resistance=10 package=THT]
  Part1 = Ambient Light Sensor (TEMT6000 Breakout Board)
  R1_(10k)1 = Resistor [tolerance=±10% resistance=4.7 package=THT]
  Part2 = Ambient Light Sensor (TEMT6000 Breakout Board)
  Part3 = Ambient Light Sensor (TEMT6000 Breakout Board)

nets:
  GND: SHT11.GND, Raspberry_Pi_B_rev2.GND, Part1.GND, Part2.GND, Part3.GND
  N1: SHT11.SCL, Raspberry_Pi_B_rev2.GPIO_23
  N2: SHT11.SDA, Raspberry_Pi_B_rev2.GPIO_24, R1_(10k).Pin_0
  VCC: SHT11.VCC, Raspberry_Pi_B_rev2.3V3, R1_(10k).Pin_1, Part1.VCC, R1_(10k)1.Pin_1, Part2.VCC, Part3.VCC
  N3: Raspberry_Pi_B_rev2.GPIO_4, Part1.S, R1_(10k)1.Pin_0, Part2.S, Part3.S

notes:
  GeauxRobot GPIO Expansion (Not Shown)
  Wiring/GPIO Labels Correct, Pins wrong on RPi
  ds18b20 x3
  Temp: Air / Case(s)
  SH10
  Soil Moisture / Temp
